# Fritzing sketch PhotocellLed (saved by Fritzing 0.9.3b)
circuit board: 8.46667cm x 5.64444cm
breadboards: 1

parts:
  Digispark1 = Digispark
  LED1 = smd LED [color="Red (633nm)" package="0805 [SMD]"]
  R1 = Resistor [tolerance=±5% resistance=330 package="0402 [SMD]"]
  R2 = PHOTOCELL [package=photocell-kit]
  R3 = Resistor [tolerance=±5% resistance=10k package="2010 [SMD]"]

nets:
  N1: Digispark1.VCC, R2.P$1
  N2: Digispark1.GND, LED1.cathode, R3.Pin_1
  N3: Digispark1.P1, R1.Pin_0
  N4: Digispark1.P3, R2.P$2, R3.Pin_0
  N5: LED1.anode, R1.Pin_1

custom parts:
  Digispark: The Digispark is an Attiny85 based microcontroller development board similar to the Arduino line, only cheaper, smaller, and a bit less powerful. With a whole host of shields to extend its functionality and the ability to use the familiar Arduino IDE the Digispark is a great way to jump into electronics, or perfect for when an Arduino is too big or too much.
